# Fritzing sketch trinketpro_w_battery (saved by Fritzing 0.9.2b)

parts:
  Part1 = Pro Trinket 3.3V
  BATT1 = 3xAAA Switchable Battery Pack w/JST connector

nets:
  N1: Part1.VBAT, BATT1.POS
  N2: Part1.GND, BATT1.NEG

custom parts:
  Pro Trinket 3.3V: The Pro Trinket 3.3V is like an Arduino Pro Mini with more pins and USB included. However, it uses 3V logic and 12MHz clock which means it's good when you want a lower-power and lower-voltage setup. Built with the common core Arduino chip, the ATmega328p, it has 18 GPIO, 2 extra analog inputs, 28K of flash, and 2K of RAM. It has onboard USB bootloading support with Optiboot support, so you can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
  3xAAA Switchable Battery Pack w/JST connector: 3xAAA Switchable Battery Pack with JST connector
