# Fritzing sketch AlternatingLights (saved by Fritzing 0.9.3b)
breadboards: 1

parts:
  Part1 = Arduino Uno (Rev3)
  S1 = SPST Switch [package=switche-dpdt]
  R1 = Resistor [tolerance=±5% resistance=10k package=THT]  # not connected
  R2 = Resistor [tolerance=±5% resistance=10k package=THT]  # not connected
  LED1 = LED - 3mm [color="Red (660nm)" package="3 mm [THT]"]
  LED2 = LED - 3mm [color="Yellow (595nm)" package="3 mm [THT]"]
  R3 = Resistor [tolerance=±5% resistance=220 package=THT]  # not connected
  R4 = Resistor [tolerance=±5% resistance=220 package=THT]

nets:
  N1: Part1.D3_PWM, R4.Pin_0
  N2: Part1.5V, S1.P
  N3: Part1.GND, LED1.cathode, LED2.cathode
  N4: LED2.anode, R4.Pin_1
