# Fritzing sketch pushbuttonAlone1 (saved by Fritzing 0.9.3b)
breadboards: 1

parts:
  Part1 = Arduino Uno (Rev3)
  R2 = Resistor [tolerance=±5% resistance=10k package="0603 [SMD]"]
  S10 = Pushbutton [package="[THT]"]

nets:
  N1: Part1.D4, R2.Pin_1, S10.Pin_3, S10.Pin_4
  N2: Part1.5V, S10.Pin_1, S10.Pin_2
