# Fritzing sketch trafficLtWSwitch (saved by Fritzing 0.9.3b)
breadboards: 1

parts:
  Part1 = Arduino Uno (Rev3)
  S1 = SPST Switch [package=switche-dpdt]
  R1 = Resistor [tolerance=±5% resistance=10k package=THT]
  R2 = Resistor [tolerance=±5% resistance=10k package=THT]
  LED1 = LED - 3mm [color="Red (660nm)" package="3 mm [THT]"]
  LED2 = LED - 3mm [color="Yellow (595nm)" package="3 mm [THT]"]
  R3 = Resistor [tolerance=±5% resistance=220 package=THT]
  R4 = Resistor [tolerance=±5% resistance=220 package=THT]
  LED3 = LED - 3mm [color="Green (570nm)" package="3 mm [THT]"]
  R5 = Resistor [tolerance=±5% resistance=220 package=THT]

nets:
  N1: Part1.D11_PWM/MOSI, S1.S
  N2: Part1.D12/MISO, S1.O, R1.Pin_1
  N3: Part1.D2, R5.Pin_0
  N4: Part1.D3_PWM, R4.Pin_0
  N5: Part1.D4, R3.Pin_0
  N6: Part1.5V, S1.P
  N7: Part1.GND, R1.Pin_0, R2.Pin_0, LED1.cathode, LED2.cathode, LED3.cathode
  N8: LED2.anode, R4.Pin_1
