# Fritzing sketch led_w_switch (saved by Fritzing 0.9.2b)
breadboards: 1

parts:
  Part1 = Arduino Uno (Rev3)
  R1 = Resistor [tolerance=±5% resistance=220 package=THT]
  S2 = SWITCH-MOMENTARY-2 [package=tactile_switch_smd-2]  # not connected
  LED1 = LED - 5mm [color="Red (635nm)" package="5 mm [THT]"]

nets:
  N1: Part1.GND, LED1.cathode
  N2: Part1.D2, R1.Pin_1
  N3: R1.Pin_0, LED1.anode
