# Fritzing sketch pushbuttonInputHigh (saved by Fritzing 0.9.3b)
breadboards: 1

parts:
  LED1 = LED - 5mm [color="Red (633nm)" package="5 mm [THT]"]
  Part1 = Arduino Uno (Rev3)
  R1 = Resistor [tolerance=±5% resistance=220 package="0603 [SMD]"]
  S10 = Pushbutton [package="[THT]"]

nets:
  N1: LED1.cathode, R1.Pin_1
  N2: LED1.anode, Part1.D10_PWM/SS
  N3: Part1.GND, R1.Pin_0, S10.Pin_1, S10.Pin_2
  N4: Part1.D4, S10.Pin_3, S10.Pin_4
