# Fritzing sketch cds_w_led (saved by Fritzing 0.9.3b)
breadboards: 1

parts:
  Part1 = Arduino Uno (Rev3)
  LED1 = LED - 3mm [color="Red (633nm)" package="3 mm [THT]"]
  R1 = Resistor [tolerance=±5% resistance=220 package=THT]
  R2 = PHOTOCELL [package=photocell-kit]  # not connected
  R3 = Resistor [tolerance=±5% resistance=22k package=THT]

nets:
  N1: Part1.A0, R3.Pin_0
  N2: Part1.D10_PWM/SS, LED1.anode
  N3: Part1.GND, R1.Pin_1, R3.Pin_1
  N4: LED1.cathode, R1.Pin_0
