# Fritzing sketch hc_sr04 (saved by Fritzing 0.9.2b)
breadboards: 1

parts:
  Part1 = Arduino Uno (Rev3)
  Part2 = SRF05 Ultrasonic Rangefinder

nets:
  N1: Part1.D11_PWM/MOSI, Part2.Echo
  N2: Part1.D12/MISO, Part2.Trig
  GND: Part1.GND, Part2.GND
  5V: Part1.5V, Part2.VCC
