# Fritzing sketch speaker_alone (saved by Fritzing 0.9.2b)
breadboards: 1

parts:
  Part1 = Arduino Uno (Rev3)
  SP1 = SPEAKER [package=pcb_mount_speaker]

nets:
  N1: Part1.GND, SP1.+
  N2: Part1.D3_PWM, SP1.-
