# Fritzing sketch speaker_w_battery (saved by Fritzing 0.9.2b)
breadboards: 1

parts:
  Part1 = Arduino Uno (Rev3)
  BATT1 = 4xAA Switchable Battery Pack w/Bare Wire
  SP1 = SPEAKER [package=pcb_mount_speaker]

nets:
  N1: Part1.D8, SP1.-
  N2: Part1.GND, BATT1.NEG
  N3: Part1.VIN, BATT1.POS

custom parts:
  4xAA Switchable Battery Pack w/Bare Wire: 4xAA Switchable Battery Pack with Bare Wire connection
