# Fritzing sketch servo-w-battery (saved by Fritzing 0.9.2b)
breadboards: 1

parts:
  Part1 = Arduino Uno (Rev3)
  J1 = Basic Servo
  BATT1 = 4xAA Switchable Battery Pack w/JST connector

nets:
  N1: Part1.D9_PWM, J1.pulse
  GND: Part1.GND, J1.gnd, BATT1.NEG
  N2: J1.vcc, BATT1.POS

custom parts:
  4xAA Switchable Battery Pack w/JST connector: 4xAA Switchable Battery Pack with JST connector
