# Fritzing sketch motor_w_all (saved by Fritzing 0.9.2b)
breadboards: 1

parts:
  Part1 = Arduino Uno (Rev3)
  BATT1 = 4xAA Switchable Battery Pack w/Bare Wire
  Q1 = NPN-Transistor [package="TO92 [THT]"]
  R1 = Resistor [tolerance=±5% resistance=1k package="0402 [SMD]"]
  U1 = DIODE-ZENER [package=diode-zener]
  M1 = DC Motor

nets:
  N1: Part1.GND, BATT1.NEG, Q1.E
  N2: Part1.D3_PWM, R1.Pin_1
  N3: BATT1.POS, U1.C, M1.pin_2
  N4: Q1.B, R1.Pin_0
  N5: Q1.C, M1.pin_1

custom parts:
  4xAA Switchable Battery Pack w/Bare Wire: 4xAA Switchable Battery Pack with Bare Wire connection
