# Fritzing sketch motor_w_resistor_battery (saved by Fritzing 0.9.2b)
breadboards: 1

parts:
  Part1 = Arduino Uno (Rev3)
  BATT1 = 4xAA Switchable Battery Pack w/Bare Wire
  R1 = Resistor [tolerance=±5% resistance=1k package="0402 [SMD]"]
  M1 = DC Motor

nets:
  N1: Part1.GND, BATT1.NEG
  N2: Part1.D3_PWM, R1.Pin_1
  N3: BATT1.POS, M1.pin_2

custom parts:
  4xAA Switchable Battery Pack w/Bare Wire: 4xAA Switchable Battery Pack with Bare Wire connection
