# Fritzing sketch solenoid_w_resistor (saved by Fritzing 0.9.2b)
breadboards: 1

parts:
  Part1 = Arduino Uno (Rev3)
  R1 = Resistor [tolerance=±5% resistance=1k package="0402 [SMD]"]
  VALVE1 = Plastic Solenoid Valve  # not connected

nets:
  N1: Part1.D3_PWM, R1.Pin_1
