# Fritzing sketch speaker_w_resistor (saved by Fritzing 0.9.2b)
breadboards: 1

parts:
  Part1 = Arduino Uno (Rev3)
  SP1 = SPEAKER [package=pcb_mount_speaker]
  R1 = Resistor [tolerance=±5% resistance=1k package="0402 [SMD]"]

nets:
  N1: Part1.GND, SP1.+
  N2: Part1.D3_PWM, R1.Pin_1
  N3: SP1.-, R1.Pin_0
