# Fritzing sketch servo-w-battery-pot (saved by Fritzing 0.9.2b)
breadboards: 1

parts:
  Part1 = Arduino Uno (Rev3)
  J1 = Basic Servo
  BATT1 = 4xAA Switchable Battery Pack w/JST connector
  U1 = POT [package=alps_pot]

nets:
  N1: Part1.A0, U1.S
  N2: Part1.D9_PWM, J1.pulse
  N3: Part1.5V, U1.E
  GND: Part1.GND, J1.gnd, BATT1.NEG, U1.A
  N4: J1.vcc, BATT1.POS

custom parts:
  4xAA Switchable Battery Pack w/JST connector: 4xAA Switchable Battery Pack with JST connector
