# Fritzing sketch motor_w_resistor (saved by Fritzing 0.9.2b)
breadboards: 1

parts:
  Part1 = Arduino Uno (Rev3)
  R1 = Resistor [tolerance=±5% resistance=1k package="0402 [SMD]"]
  M1 = DC Motor

nets:
  N1: Part1.GND, M1.pin_1
  N2: Part1.D3_PWM, R1.Pin_1
  N3: R1.Pin_0, M1.pin_2
