# Fritzing sketch pir_w_led (saved by Fritzing 0.9.2b)
breadboards: 1

parts:
  Part1 = Arduino Uno (Rev3) - ICSP
  PIR1 = PIR sensor
  LED1 = smd LED [color="Red (633nm)" package="0603 [SMD]"]
  R1 = Resistor [tolerance=±5% resistance=220 package="2512 [SMD]"]

nets:
  N1: Part1.D2, PIR1.SIG
  N2: Part1.D6_PWM, LED1.anode
  5V: Part1.5V, PIR1.VDD
  N3: PIR1.GND, R1.Pin_1
  N4: LED1.cathode, R1.Pin_0
