# Fritzing sketch servo_w_leds (saved by Fritzing 0.9.3b)
breadboards: 1

parts:
  R1 = Resistor [tolerance=±5% resistance=220 package="0603 [SMD]"]
  R2 = Resistor [tolerance=±5% resistance=220 package="0603 [SMD]"]
  Part1 = Arduino Uno (Rev3)
  LED2 = smd LED [color="Green (570nm)" package="1206 [SMD]"]
  J1 = Basic Servo
  R3 = PHOTOCELL [package=photocell-kit]  # not connected
  LED3 = smd LED [color="Red (635nm)" package="1206 [SMD]"]
  R4 = Resistor [tolerance=±5% resistance=4.7k package="0603 [SMD]"]
  VCC1 = Battery block 9V

nets:
  N1: R1.Pin_0, LED2.cathode
  GND: R1.Pin_1, R2.Pin_1, Part1.GND, J1.gnd, R4.Pin_1, VCC1.-
  N2: R2.Pin_0, LED3.cathode
  N3: Part1.D9_PWM, J1.pulse
  N4: Part1.D2, LED2.anode
  N5: Part1.D4, LED3.anode
  5V: Part1.5V, J1.vcc
  N6: Part1.VIN, VCC1.+
