# Fritzing sketch solenoid_w_mosfet_gate (saved by Fritzing 0.9.2b)
breadboards: 1

parts:
  Part1 = Arduino Uno (Rev3)
  BATT1 = 4xAA Switchable Battery Pack w/Bare Wire
  R1 = Resistor [tolerance=±5% resistance=1k package="0402 [SMD]"]
  U1 = DIODE-ZENER [package=diode-zener]
  Q2 = MOSFET-NCHANNEL [package=to220v]
  VALVE1 = Plastic Solenoid Valve
  Q3 = NPN-Transistor [package="SOT-23 [SMD]"]
  R2 = Resistor [tolerance=±5% resistance=220 package="0402 [SMD]"]

nets:
  N1: Part1.GND, BATT1.NEG, Q2.S, Q3.1
  N2: Part1.D3_PWM, R1.Pin_0
  N3: BATT1.POS, U1.C, VALVE1.no_name_yet#2, R2.Pin_1
  N4: R1.Pin_1, Q3.0
  N5: Q2.G, Q3.2, R2.Pin_0
  N6: Q2.D, VALVE1.no_name_yet#1

custom parts:
  4xAA Switchable Battery Pack w/Bare Wire: 4xAA Switchable Battery Pack with Bare Wire connection
