# Fritzing sketch solenoid_w_speaker (saved by Fritzing 0.9.2b)
breadboards: 1

parts:
  Part1 = Arduino Uno (Rev3) - ICSP
  LED1 = smd LED [color="Red (633nm)" package="0603 [SMD]"]
  R1 = Resistor [tolerance=±5% resistance=220 package=THT]
  R2 = Resistor [tolerance=±5% resistance=220 package=THT]
  R3 = Resistor [tolerance=±5% resistance=220 package=THT]
  Q1 = NPN-Transistor [package="TO92 [THT]"]
  SP1 = SPEAKER [package=pcb_mount_speaker]
  Q2 = Basic FET N-Channel [package="DPak [SMD]"]
  VALVE1 = Plastic Solenoid Valve
  U1 = DIODE-ZENER [package=diode-zener]
  J1 = ATX24 Pin Power Supply Connector [package=atx24_right_angle]
  VCC1 = Battery block 9V

nets:
  N1: Part1.D8, R3.Pin_0
  GND: Part1.GND, LED1.cathode, Q1.E, Q2.source, J1.GND, VCC1.-
  N2: Part1.D3_PWM, R1.Pin_1
  N3: Part1.D7, R2.Pin_1
  N4: Part1.VIN, VCC1.+
  N5: LED1.anode, R1.Pin_0
  N6: R2.Pin_0, Q1.B
  N7: R3.Pin_1, Q2.Gate
  N8: Q1.C, SP1.+
  N9: Q2.drain, VALVE1.no_name_yet#1
  N10: VALVE1.no_name_yet#2, U1.C, J1.12V
